# Fritzing sketch amp (saved by Fritzing 1.0.8)
breadboards: 2

parts:
  Part2 = Lithium Ion Cylindrical Battery 3.7v 2200mAh [part_number=1781]  # not connected
  S1 = Toggle Switch [package=THT]
  Part3 = Adafruit PowerBoost 1000C (headers) [part_number="Adafruit #2465"]
  SOM2 = Daisy Seed [chip_label=IC package="DIP (Dual Inline) [THT]"]
  Part4 = Adafruit MAX98306 Stereo 3.7W Class D Audio Amplifier [part_number="Adafruit #987"]
  SP1 = SPEAKER [package=pcb_mount_speaker]
  SP2 = SPEAKER [package=pcb_mount_speaker]

nets:
  GND: S1.L1, Part3.GND, SOM2.pin_20, SOM2.pin_40, Part4.GND, Part4.IN_RIGHT-, Part4.IN_LEFT-
  N1: S1.COM, Part3.ENABLE
  N2: S1.L2, Part3.VBAT
  N3: Part3.5.0V, SOM2.pin_39, Part4.VDD
  N4: SOM2.pin_18, Part4.IN_LEFT+
  N5: SOM2.pin_19, Part4.IN_RIGHT+
  N6: Part4.LOUT-, SP1.+
  N7: Part4.LOUT+, SP1.-
  N8: Part4.ROUT+, SP2.-
  N9: Part4.ROUT-, SP2.+

custom parts:
  Lithium Ion Cylindrical Battery 3.7v 2200mAh: This lithium ion battery has a capacity of 2200mAh and a protection circuit that provides over-voltage, under-voltage and over-current protection. This cell can provide 2C of peak current (4400mA). Note that these batteries are not designed to sustain such high loads, we suggest keeping any constant current draw under about 0.5C (1 Amp).
  Adafruit PowerBoost 1000C (headers): PowerBoost 1000C is the perfect power supply for your portable project! With a built-in load-sharing battery charger circuit, you'll be able to keep your power-hungry project running even while recharging the battery! This little DC/DC boost converter module can be powered by any 3.7V LiIon/LiPoly battery, and convert the battery output to 5.2V DC for running your 5V projects.
  Daisy Seed: Daisy is an embedded platform for music. It features everything you need for creating high fidelity audio hardware devices. Just plug in a USB cable and start making sound! No soldering required.
  Adafruit MAX98306 Stereo 3.7W Class D Audio Amplifier: This incredibly small stereo amplifier is surprisingly powerful - able to deliver 2 x 3.7W channels into 3 ohm impedance speakers. Inside the miniature chip is a class D controller, able to run from 2.7V-5.5VDC. Since the amp is a class D, its incredibly efficient (over 90% efficient when driving an 8Ω speaker at over a Watt) - making it perfect for portable and battery-powered projects. It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
