# Fritzing sketch fsr (saved by Fritzing 1.0.8)
breadboards: 1

parts:
  SOM1 = Daisy Seed [chip_label=IC package="DIP (Dual Inline) [THT]"]
  R2 = Resistor [tolerance=±5% resistance=10k package="0402 [SMD]"]
  J1 = Basic Force Sensing Resistor (FSR) [package=THT]

nets:
  N1: SOM1.pin_20, SOM1.pin_40, R2.Pin_1
  N2: SOM1.pin_22, R2.Pin_0, J1.pin_1
  N3: SOM1.pin_38, J1.pin_0

custom parts:
  Daisy Seed: Daisy is an embedded platform for music. It features everything you need for creating high fidelity audio hardware devices. Just plug in a USB cable and start making sound! No soldering required.
