# Fritzing sketch hello_world (saved by Fritzing 1.0.8)
breadboards: 1

parts:
  SOM1 = Daisy Seed [chip_label=IC package="DIP (Dual Inline) [THT]"]
  S1 = Momentary Switch [package=ksa_sealed_tac_switch]
  R1 = Resistor [tolerance=±5% resistance=10k package="2010 [SMD]"]

nets:
  N1: SOM1.pin_11, S1.2
  N2: SOM1.pin_20, SOM1.pin_40, R1.Pin_0
  N3: SOM1.pin_38, S1.3
  N4: S1.1, R1.Pin_1

custom parts:
  Daisy Seed: Daisy is an embedded platform for music. It features everything you need for creating high fidelity audio hardware devices. Just plug in a USB cable and start making sound! No soldering required.
