# Fritzing sketch hello_world_panel_button (saved by Fritzing 1.0.8)
breadboards: 1

parts:
  SOM1 = Daisy Seed [chip_label=IC package="DIP (Dual Inline) [THT]"]
  S2 = Square Pushbutton

nets:
  N1: SOM1.pin_11, S2.leg1
  N2: SOM1.pin_20, SOM1.pin_40, S2.leg0

custom parts:
  Daisy Seed: Daisy is an embedded platform for music. It features everything you need for creating high fidelity audio hardware devices. Just plug in a USB cable and start making sound! No soldering required.
