# Fritzing sketch imu (saved by Fritzing 1.0.8)
breadboards: 1

parts:
  SOM1 = Daisy Seed [chip_label=IC package="DIP (Dual Inline) [THT]"]
  Part1 = Adafruit ICM20948

nets:
  N1: SOM1.pin_12, Part1.SCK/SCL
  N2: SOM1.pin_13, Part1.SDI/SDA
  N3: SOM1.pin_20, SOM1.pin_40, Part1.GND
  N4: SOM1.pin_38, Part1.VIN

custom parts:
  Daisy Seed: Daisy is an embedded platform for music. It features everything you need for creating high fidelity audio hardware devices. Just plug in a USB cable and start making sound! No soldering required.
