# Fritzing sketch input_jack (saved by Fritzing 1.0.8)
breadboards: 1

parts:
  SOM1 = Daisy Seed [chip_label=IC package="DIP (Dual Inline) [THT]"]
  J1 = 1/4 inch mono jack (open frame) [package=audio-jack-6.5mm-open-frame]

nets:
  N1: SOM1.pin_17, J1.Tip
  N2: SOM1.pin_20, SOM1.pin_40, J1.Sleeve

custom parts:
  Daisy Seed: Daisy is an embedded platform for music. It features everything you need for creating high fidelity audio hardware devices. Just plug in a USB cable and start making sound! No soldering required.
  1/4 inch mono jack (open frame): 1/4 inch mono Audio Jack Open-frame 1/4 inch mono (TS) jack, Switchcraft 11 style. Breadboard image redrawn for AC ARHA/MUSI 274; schematic and PCB from vanepp's 1/4 inch mono jack.
