# Fritzing sketch led (saved by Fritzing 1.0.8)
breadboards: 1

parts:
  SOM1 = Daisy Seed [chip_label=IC package="DIP (Dual Inline) [THT]"]
  LED1 = LED - 5mm [color="Red (633nm)" current=0.030A package="5 mm [THT]"]
  R1 = Resistor [tolerance=±5% resistance=220 package="2010 [SMD]"]

nets:
  N1: SOM1.pin4, LED1.anode
  N2: SOM1.pin_20, SOM1.pin_40, R1.Pin_1
  N3: LED1.cathode, R1.Pin_0

custom parts:
  Daisy Seed: Daisy is an embedded platform for music. It features everything you need for creating high fidelity audio hardware devices. Just plug in a USB cable and start making sound! No soldering required.
