# Fritzing sketch photocell (saved by Fritzing 1.0.8)
breadboards: 1

parts:
  SOM1 = Daisy Seed [chip_label=IC package="DIP (Dual Inline) [THT]"]
  R2 = Resistor [tolerance=±5% resistance=10k package="0402 [SMD]"]
  R1 = PHOTOCELL [package=photocell-kit]

nets:
  N1: SOM1.pin_20, SOM1.pin_40, R2.Pin_1
  N2: SOM1.pin_22, R2.Pin_0, R1.P$2
  N3: SOM1.pin_38, R1.P$1

custom parts:
  Daisy Seed: Daisy is an embedded platform for music. It features everything you need for creating high fidelity audio hardware devices. Just plug in a USB cable and start making sound! No soldering required.
