# Fritzing sketch potentiometer (saved by Fritzing 1.0.8)
breadboards: 1

parts:
  SOM1 = Daisy Seed [chip_label=IC package="DIP (Dual Inline) [THT]"]
  U1 = POT [knob_status=50% power=0.5W package=pot_mammoth]

nets:
  N1: SOM1.pin_20, SOM1.pin_40, U1.E
  N2: SOM1.pin_22, U1.A
  N3: SOM1.pin_38, U1.S

custom parts:
  Daisy Seed: Daisy is an embedded platform for music. It features everything you need for creating high fidelity audio hardware devices. Just plug in a USB cable and start making sound! No soldering required.
