# Fritzing sketch powerboost (saved by Fritzing 1.0.8)
breadboards: 2

parts:
  Part2 = Lithium Ion Cylindrical Battery 3.7v 2200mAh [part_number=1781]  # not connected
  S1 = Toggle Switch [package=THT]
  Part3 = Adafruit PowerBoost 1000C (headers) [part_number="Adafruit #2465"]
  SOM2 = Daisy Seed [chip_label=IC package="DIP (Dual Inline) [THT]"]

nets:
  N1: S1.L1, Part3.GND, SOM2.pin_20, SOM2.pin_40
  N2: S1.COM, Part3.ENABLE
  N3: S1.L2, Part3.VBAT
  N4: Part3.5.0V, SOM2.pin_39

custom parts:
  Lithium Ion Cylindrical Battery 3.7v 2200mAh: This lithium ion battery has a capacity of 2200mAh and a protection circuit that provides over-voltage, under-voltage and over-current protection. This cell can provide 2C of peak current (4400mA). Note that these batteries are not designed to sustain such high loads, we suggest keeping any constant current draw under about 0.5C (1 Amp).
  Adafruit PowerBoost 1000C (headers): PowerBoost 1000C is the perfect power supply for your portable project! With a built-in load-sharing battery charger circuit, you'll be able to keep your power-hungry project running even while recharging the battery! This little DC/DC boost converter module can be powered by any 3.7V LiIon/LiPoly battery, and convert the battery output to 5.2V DC for running your 5V projects.
  Daisy Seed: Daisy is an embedded platform for music. It features everything you need for creating high fidelity audio hardware devices. Just plug in a USB cable and start making sound! No soldering required.
