# Fritzing sketch stereo_jack (saved by Fritzing 1.0.8)
breadboards: 1

parts:
  SOM1 = Daisy Seed [chip_label=IC package="DIP (Dual Inline) [THT]"]
  J2 = 3.5mm stereo jack (panel mount) [part_number="Adafruit 3692" package="panel mount, solder tabs"]

nets:
  N1: SOM1.pin_16, J2.Tip
  N2: SOM1.pin_17, J2.Ring
  N3: SOM1.pin_20, SOM1.pin_40, J2.Sleeve

custom parts:
  Daisy Seed: Daisy is an embedded platform for music. It features everything you need for creating high fidelity audio hardware devices. Just plug in a USB cable and start making sound! No soldering required.
  3.5mm stereo jack (panel mount): Panel-mount 1/8 inch (3.5mm) stereo TRS jack with three solder tabs, Adafruit 3692 style. Tip = left, ring = right, sleeve = ground. Check which tab is which with a meter: the sleeve tab is the one with continuity to the threaded bushing.
